# Fritzing sketch QuadcopterArduinoMega_Shield (saved by Fritzing 0.9.1b)
circuit board: 10.9355cm x 5.88386cm
breadboards: 1

parts:
  Part1 = Arduino Mega 2560 (Rev3)
  BAT1 = LIPO-2000mAh [package=lipo-2000]
  J2 = Basic Servo
  J3 = Basic Servo
  J4 = Basic Servo
  J5 = Basic Servo
  MPU9150 = MPU-6050 Board GY-521 [form="♀ (female)" package=THT]
  MicroSD_Adapter = SparkFun - microSD Transflash

nets:
  N1: Part1.D21/SCL, Part1.SCL, MPU9150.pin4
  N2: Part1.D20/SDA, Part1.SDA, MPU9150.pin3
  GND: Part1.GND, MPU9150.pin2, MicroSD_Adapter.GND
  N3: Part1.3V3, MPU9150.pin1, MPU9150.pin7
  N4: Part1.D2_PWM, J2.pulse
  N5: Part1.D3_PWM, J3.pulse
  N6: Part1.D4_PWM, J5.pulse
  N7: Part1.D5_PWM, J4.pulse
  N8: Part1.D22, MPU9150.pin5
  N9: Part1.D50, MicroSD_Adapter.MISO
  N10: Part1.D51, MicroSD_Adapter.MOSI
  N11: Part1.D52, MicroSD_Adapter.SCK
  N12: Part1.D53, MicroSD_Adapter.CS#1
  VCC: BAT1.+, J2.vcc, J3.vcc, J4.vcc, J5.vcc
  GND_2: BAT1.-, J2.gnd, J3.gnd, J4.gnd, J5.gnd

custom parts:
  MPU-6050 Board GY-521: Acelerometro y Giroscopio MPU-6050 Board GY-521
  SparkFun - microSD Transflash: https://www.sparkfun.com/products/544 Breakout board for the microSD socket that is not much bigger than your fingernail. Compatible with the SPI interface found on any SD card, this tiny form factor was created for cell phone storage and is perfect for your next MP3 project! Board comes fully assembled and tested. The bare socket is available.
